# Fritzing sketch 00.LEDbarKristianMedri (saved by Fritzing 0.9.4)
circuit board: 5.70353cm x 4.44972cm
breadboards: 1

parts:
  J1 = STM32F103C8T6 blue mini board
  B2 = female pin header, 6 pins [form="♀ (female)"]
  LEDbar = LED_BARGRAPH_10 [package=led_bargaph_10]
  B3 = female pin header, 2 pins [form="♀ (female)"]
  R12 = Resistor [tolerance=±5% resistance=220 package="0603 [SMD]"]
  R13 = Resistor [tolerance=±5% resistance=220 package="0603 [SMD]"]
  R14 = Resistor [tolerance=±5% resistance=220 package="0603 [SMD]"]
  R15 = Resistor [tolerance=±5% resistance=220 package="0603 [SMD]"]
  R16 = Resistor [tolerance=±5% resistance=220 package="0603 [SMD]"]
  R17 = Resistor [tolerance=±5% resistance=220 package="0603 [SMD]"]
  R18 = Resistor [tolerance=±5% resistance=220 package="0603 [SMD]"]
  R19 = Resistor [tolerance=±5% resistance=220 package="0603 [SMD]"]
  R20 = Resistor [tolerance=±5% resistance=220 package="0603 [SMD]"]
  R21 = Resistor [tolerance=±5% resistance=220 package="0603 [SMD]"]
  B4 = female pin header, 2 pins [form="♀ (female)"]

nets:
  N1: J1.A9, B2.pin2
  N2: J1.A10, B2.pin3
  N3: J1.G, B2.pin6
  N4: J1.3.3V, B4.pin1
  N5: J1.A0, LEDbar.A_C
  N6: J1.A1, LEDbar.B_C
  N7: J1.A2, LEDbar.C_C
  N8: J1.A3, LEDbar.D_C
  N9: J1.A4, LEDbar.E_C
  N10: J1.A5, LEDbar.F_C
  N11: J1.A6, LEDbar.G_C
  N12: J1.A7, LEDbar.H_C
  N13: LEDbar.A_A, R12.Pin_0
  N14: LEDbar.B_A, R13.Pin_0
  N15: LEDbar.C_A, R14.Pin_0
  N16: LEDbar.D_A, R15.Pin_0
  N17: LEDbar.E_A, R16.Pin_0
  N18: LEDbar.F_A, R17.Pin_0
  N19: LEDbar.G_A, R18.Pin_0
  N20: LEDbar.H_A, R19.Pin_0
  N21: LEDbar.I_A, R20.Pin_0
  N22: LEDbar.J_A, R21.Pin_0
  N23: LEDbar.J_C, B3.pin1
  N24: LEDbar.I_C, B3.pin2
  N25: R12.Pin_1, R13.Pin_1, R14.Pin_1, R15.Pin_1, R16.Pin_1, R17.Pin_1, R18.Pin_1, R19.Pin_1, R20.Pin_1, R21.Pin_1, B4.pin2

notes:
  PA0
  G
  00.LEDbarKristianMedri.fzz
  G G3.3
  VBAT
  5V G3.3
  RX
  TX
